// Logisim project lab06.circ as structural Verilog: 13 circuits, main circuit main
module main (
  input  [15:0] in_1,
  input  [3:0] in_2,
  input  in_3,
  input  in_4,
  input  [7:0] in_5,
  output [15:0] out_6,
  output out_7,
  output out_8,
  output [7:0] out_9
);

  NAND1 nand1_1 (.in_1(in_3), .in_2(in_4), .out_3(out_7));
  Ex4 ex4_1 (.In1(in_5), .Out1(out_8), .Out2(out_9));
  Rotr rotr_1 (.InputA(in_1), .InputB(in_2), .out_3(out_6));
endmodule

module NAND1 (
  input  in_1,
  input  in_2,
  output out_3
);

  wire and_1_out;

  and and_1 (and_1_out, in_1, in_2);
  not not_1 (out_3, and_1_out);
endmodule

module NOR1 (
  input  in_1,
  input  in_2,
  output out_3
);

  wire or_1_out;

  or or_1 (or_1_out, in_1, in_2);
  not not_1 (out_3, or_1_out);
endmodule

module XOR1 (
  input  in_1,
  input  in_2,
  output out_3
);

  wire nand1_1_out_3, or_1_out;

  NAND1 nand1_1 (.in_1(in_1), .in_2(in_2), .out_3(nand1_1_out_3));
  or or_1 (or_1_out, in_2, in_1);
  and and_1 (out_3, nand1_1_out_3, or_1_out);
endmodule

module MUX21 (
  input  input1,
  input  inputS,
  input  input2,
  output out_4
);

  wire and_1_out, and_2_out, not_1_out;

  not not_1 (not_1_out, inputS);
  and and_1 (and_1_out, not_1_out, input1);
  and and_2 (and_2_out, inputS, input2);
  or or_1 (out_4, and_1_out, and_2_out);
endmodule

module MUX41 (
  input  inputA,
  input  inputB,
  input  inputS0,
  input  inputS1,
  input  inputC,
  input  inputD,
  output out_7
);

  wire mux21_1_out_4, mux21_2_out_4;

  MUX21 mux21_1 (.input1(inputA), .inputS(inputS0), .input2(inputB), .out_4(mux21_1_out_4));
  MUX21 mux21_2 (.input1(inputC), .inputS(inputS0), .input2(inputD), .out_4(mux21_2_out_4));
  MUX21 mux21_3 (.input1(mux21_1_out_4), .inputS(inputS1), .input2(mux21_2_out_4), .out_4(out_7));
endmodule

module AddMachine (
  output [7:0] out_1,
  output [7:0] out_2
);

  wire clock_1_out;

  Adder adder_1 (.a(8'h1), .b(out_2), .out(out_1));  // open: cin, cout
  Clock clock_1 (.out(clock_1_out));
  Multiplexer #(.enable("false")) multiplexer_1 ();  // open: in0, in1, out, sel
  Register register_1 (.D(out_1), .clk(clock_1_out), .Q(out_2));  // open: en, clr
endmodule

module Ex4 (
  input  [7:0] In1,
  output Out1,
  output [7:0] Out2
);

  not not_1 (Out2[7], In1[7]);
  and and_1 (Out1, In1[0], In1[7]);

  assign Out2[6:0] = In1[6:0];

  // Other names for the same wires on the sheet: Bit7 = In1[7]; Bit0 = In1[0]; Bit16[5:0] = In1[6:1]
endmodule

module Rotr (
  input  [15:0] InputA,
  input  [3:0] InputB,
  output [15:0] out_3
);

  wire [15:0] shifteight_1_out_3, shiftfour_1_out_3, shifttwo_1_out_3;

  shiftEight shifteight_1 (.inputA(InputA), .bit3(InputB[3]), .out_3(shifteight_1_out_3));
  shiftFour shiftfour_1 (.inputA(shifteight_1_out_3), .bit2(InputB[2]), .out_3(shiftfour_1_out_3));
  shiftTwo shifttwo_1 (.inputA(shiftfour_1_out_3), .bit1(InputB[1]), .out_3(shifttwo_1_out_3));
  shift1 shift1_1 (.shiftOne(shifttwo_1_out_3), .bit0(InputB[0]), .out_3(out_3));

  // Other names for the same wires on the sheet: bit0 = InputB[0]; bit1 = InputB[1]; bit2 = InputB[2];
  //   bit3 = InputB[3]
endmodule

module shiftEight (
  input  [15:0] inputA,
  input  bit3,
  output [15:0] out_3
);

  Multiplexer #(.width(16), .enable("false")) multiplexer_1 (
    .in0(inputA), .in1({inputA[7:0], inputA[15:8]}), .out(out_3), .sel(bit3));

  // Other names for the same wires on the sheet: second[7:0] = inputA[15:8]; first[7:0] = inputA[7:0]
endmodule

module shiftFour (
  input  [15:0] inputA,
  input  bit2,
  output [15:0] out_3
);

  Multiplexer #(.width(16), .enable("false")) multiplexer_1 (
    .in0(inputA), .in1({inputA[3:0], inputA[15:4]}), .out(out_3), .sel(bit2));

  // Other names for the same wires on the sheet: second[11:0] = inputA[15:4]; first[3:0] = inputA[3:0]
endmodule

module shiftTwo (
  input  [15:0] inputA,
  input  bit1,
  output [15:0] out_3
);

  Multiplexer #(.width(16), .enable("false")) multiplexer_1 (
    .in0(inputA), .in1({inputA[1:0], inputA[15:2]}), .out(out_3), .sel(bit1));

  // Other names for the same wires on the sheet: second[13:0] = inputA[15:2]; first[1:0] = inputA[1:0]
endmodule

module shift1 (
  input  [15:0] shiftOne,
  input  bit0,
  output [15:0] out_3
);

  Multiplexer #(.width(16), .enable("false")) multiplexer_1 (
    .in0(shiftOne), .in1({shiftOne[0], shiftOne[15:1]}), .out(out_3), .sel(bit0));

  // Other names for the same wires on the sheet: second[14:0] = shiftOne[15:1]; first = shiftOne[0]
endmodule
